// Logisim project Suivi de ligne.circ as structural Verilog: 3 circuits, main circuit main
module main (
);

  Suivi_de_ligne suivi_de_ligne_1 ();  // open: C1, C2, C3, C4, C5, C6, C7, C8, TG, TD, A, R
  Suivi_de_ligne_2_0 suivi_de_ligne_2_0_1 ();  // open: C1, C2, C3, C4, C5, C6, C7, C8, TG, TD, A, R
endmodule

module Suivi_de_ligne (
  input  C1,
  input  C2,
  input  C3,
  input  C4,
  input  C5,
  input  C6,
  input  C7,
  input  C8,
  output TG,
  output TD,
  output A,
  output R
);

  wire and_1_out, and_2_out, and_3_out, and_4_out, and_5_out, and_6_out, and_7_out, and_8_out, and_9_out,
       and_10_out, and_11_out, and_12_out, and_13_out, and_14_out, not_1_out, not_2_out, not_3_out,
       not_4_out, not_5_out, not_6_out, not_7_out, not_8_out, not_9_out, not_10_out, not_11_out, not_12_out,
       not_13_out, not_14_out, not_15_out, not_16_out, not_17_out, not_18_out, not_19_out, not_20_out,
       not_21_out, not_22_out, not_23_out, not_24_out, not_25_out, not_26_out, not_27_out, not_28_out,
       not_29_out, not_30_out, not_31_out, not_32_out, not_33_out, not_34_out, not_35_out, not_36_out,
       not_37_out, not_38_out, not_39_out, not_40_out, not_41_out, not_42_out, not_43_out, not_44_out,
       not_45_out, not_46_out, not_47_out, not_48_out, not_49_out, not_50_out, not_51_out, not_52_out,
       not_53_out, not_54_out, not_55_out, not_56_out, not_57_out, not_58_out, not_59_out, not_60_out,
       not_61_out, not_62_out, not_63_out, not_64_out, not_65_out, not_66_out, not_67_out, not_68_out,
       not_69_out, not_70_out, not_71_out, not_72_out, not_73_out, not_74_out, not_75_out, not_76_out,
       not_77_out, not_78_out, not_79_out, not_80_out, or_1_out, or_2_out, or_3_out, or_4_out, or_5_out,
       or_6_out, or_7_out, or_8_out, or_9_out, or_10_out, or_11_out, or_12_out;

  or or_1 (or_1_out, C1, C3, C4);
  or or_2 (or_2_out, C7, not_1_out);
  not not_1 (not_1_out, C8);
  or or_3 (or_3_out, C6, not_2_out);
  not not_2 (not_2_out, C7);
  or or_4 (or_4_out, C5, not_3_out);
  not not_3 (not_3_out, C6);
  not not_4 (not_4_out, C5);
  or or_5 (or_5_out, C3, not_4_out, C6);
  or or_6 (or_6_out, C4, not_5_out);
  not not_5 (not_5_out, C5);
  not not_6 (not_6_out, C3);
  or or_7 (or_7_out, C2, not_6_out, C7);
  not not_7 (not_7_out, C2);
  or or_8 (or_8_out, C1, not_7_out, C3);
  not not_8 (not_8_out, C2);
  or or_9 (or_9_out, C1, not_8_out, not_9_out);
  not not_9 (not_9_out, C7);
  not not_10 (not_10_out, C1);
  or or_10 (or_10_out, not_10_out, not_11_out);
  not not_11 (not_11_out, C8);
  not not_12 (not_12_out, C1);
  or or_11 (or_11_out, not_12_out, C2, not_13_out);
  not not_13 (not_13_out, C4);
  not not_14 (not_14_out, C1);
  or or_12 (or_12_out, not_14_out, C3, not_15_out);
  not not_15 (not_15_out, C4);
  not not_16 (not_16_out, C1);
  not not_17 (not_17_out, C2);
  not not_18 (not_18_out, C3);
  not not_19 (not_19_out, C4);
  not not_20 (not_20_out, C5);
  not not_21 (not_21_out, C6);
  not not_22 (not_22_out, C1);
  not not_23 (not_23_out, C2);
  not not_24 (not_24_out, C3);
  not not_25 (not_25_out, C4);
  not not_26 (not_26_out, C5);
  not not_27 (not_27_out, C1);
  not not_28 (not_28_out, C2);
  not not_29 (not_29_out, C3);
  not not_30 (not_30_out, C4);
  not not_31 (not_31_out, C8);
  not not_32 (not_32_out, C1);
  not not_33 (not_33_out, C2);
  not not_34 (not_34_out, C3);
  not not_35 (not_35_out, C4);
  not not_36 (not_36_out, C1);
  not not_37 (not_37_out, C2);
  not not_38 (not_38_out, C3);
  not not_39 (not_39_out, C4);
  not not_40 (not_40_out, C7);
  not not_41 (not_41_out, C8);
  not not_42 (not_42_out, C1);
  not not_43 (not_43_out, C2);
  not not_44 (not_44_out, C5);
  not not_45 (not_45_out, C6);
  not not_46 (not_46_out, C7);
  not not_47 (not_47_out, C8);
  not not_48 (not_48_out, C1);
  not not_49 (not_49_out, C2);
  not not_50 (not_50_out, C6);
  not not_51 (not_51_out, C7);
  not not_52 (not_52_out, C8);
  not not_53 (not_53_out, C1);
  not not_54 (not_54_out, C3);
  not not_55 (not_55_out, C4);
  not not_56 (not_56_out, C5);
  not not_57 (not_57_out, C6);
  not not_58 (not_58_out, C7);
  not not_59 (not_59_out, C8);
  not not_60 (not_60_out, C1);
  not not_61 (not_61_out, C1);
  not not_62 (not_62_out, C2);
  not not_63 (not_63_out, C3);
  not not_64 (not_64_out, C4);
  not not_65 (not_65_out, C5);
  not not_66 (not_66_out, C6);
  not not_67 (not_67_out, C7);
  not not_68 (not_68_out, C8);
  not not_69 (not_69_out, C1);
  not not_70 (not_70_out, C2);
  not not_71 (not_71_out, C3);
  not not_72 (not_72_out, C6);
  not not_73 (not_73_out, C7);
  not not_74 (not_74_out, C8);
  not not_75 (not_75_out, C1);
  not not_76 (not_76_out, C2);
  not not_77 (not_77_out, C7);
  not not_78 (not_78_out, C8);
  not not_79 (not_79_out, C1);
  not not_80 (not_80_out, C8);
  and and_1 (and_1_out, not_16_out, not_17_out, not_18_out, not_19_out, not_20_out, not_21_out, C8);
  and and_2 (and_2_out, not_22_out, not_23_out, not_24_out, not_25_out, not_26_out, C7);
  and and_3 (and_3_out, not_27_out, not_28_out, not_29_out, not_30_out, C6, not_31_out);
  and and_4 (and_4_out, not_32_out, not_33_out, not_34_out, not_35_out, C6, C7);
  and and_5 (and_5_out, not_36_out, not_37_out, not_38_out, not_39_out, C5, not_40_out, not_41_out);
  and and_6 (and_6_out, not_42_out, not_43_out, C3, not_44_out, not_45_out, not_46_out, not_47_out);
  and and_7 (and_7_out, not_48_out, not_49_out, C3, C4, not_50_out, not_51_out, not_52_out);
  and and_8 (and_8_out, not_53_out, C2, not_54_out, not_55_out, not_56_out, not_57_out, not_58_out, not_59_out);
  and and_9 (and_9_out, not_60_out, C2, C3, C4, C5, C6, C7, C8);
  and and_10 (and_10_out, not_61_out, not_62_out, not_63_out, not_64_out, not_65_out, not_66_out, not_67_out, not_68_out);
  and and_11 (and_11_out, not_69_out, not_70_out, not_71_out, C4, C5, not_72_out, not_73_out, not_74_out);
  and and_12 (and_12_out, not_75_out, not_76_out, C3, C4, C5, C6, not_77_out, not_78_out);
  and and_13 (and_13_out, not_79_out, C2, C3, C4, C5, C6, C7, not_80_out);
  and and_14 (and_14_out, C1, C2, C3, C4, C5, C6, C7, C8);
  and and_15 (TG, or_1_out, or_2_out, or_3_out, or_4_out, or_5_out, or_6_out, or_7_out, or_8_out, or_9_out, or_10_out, or_11_out, or_12_out);
  or or_13 (TD, and_1_out, and_2_out, and_3_out, and_4_out, and_5_out, and_6_out, and_7_out, and_8_out, and_9_out);
  or or_14 (A, and_10_out, and_11_out);
  or or_15 (R, and_12_out, and_13_out, and_14_out);
endmodule

module Suivi_de_ligne_2_0 (
  input  C1,
  input  C2,
  input  C3,
  input  C4,
  input  C5,
  input  C6,
  input  C7,
  input  C8,
  output TG,
  output TD,
  output A,
  output R
);

  wire and_1_out, and_2_out, and_3_out, and_4_out, and_5_out, and_6_out, and_7_out, and_8_out, and_9_out,
       and_10_out, and_11_out, not_1_out, not_2_out, not_3_out, not_4_out, not_5_out, not_6_out, not_7_out,
       not_8_out, not_9_out, not_10_out, not_11_out, not_12_out, not_13_out, not_14_out, not_15_out,
       not_16_out, not_17_out, not_18_out, not_19_out, not_20_out, not_21_out, not_22_out, not_23_out,
       not_24_out, not_25_out, not_26_out, not_27_out, not_28_out, not_29_out, not_30_out, not_31_out,
       not_32_out, not_33_out, not_34_out, not_35_out, not_36_out, not_37_out, not_38_out, not_39_out,
       not_40_out, not_41_out, not_42_out, not_43_out, not_44_out, not_45_out, not_46_out, not_47_out,
       not_48_out, not_49_out, not_50_out, not_51_out, not_52_out, not_53_out, not_54_out, not_55_out,
       not_56_out, not_57_out, not_58_out, not_59_out, not_60_out, not_61_out, not_62_out, not_63_out,
       not_64_out, not_65_out, not_66_out, not_67_out, not_68_out, not_69_out, not_70_out, not_71_out,
       not_72_out, not_73_out, not_74_out, or_1_out, or_2_out, or_3_out, or_4_out, or_5_out, or_6_out,
       or_7_out, or_8_out, or_9_out, or_10_out, or_11_out, or_12_out;

  or or_1 (or_1_out, C1, C3, C4);
  or or_2 (or_2_out, C7, not_1_out);
  not not_1 (not_1_out, C8);
  or or_3 (or_3_out, C6, not_2_out);
  not not_2 (not_2_out, C7);
  or or_4 (or_4_out, C5, not_3_out);
  not not_3 (not_3_out, C6);
  not not_4 (not_4_out, C5);
  or or_5 (or_5_out, C3, not_4_out, C6);
  or or_6 (or_6_out, C4, not_5_out);
  not not_5 (not_5_out, C5);
  or or_7 (or_7_out, C2, not_6_out, C7);
  not not_6 (not_6_out, C3);
  or or_8 (or_8_out, C1, not_7_out, C3);
  not not_7 (not_7_out, C2);
  not not_8 (not_8_out, C2);
  or or_9 (or_9_out, C1, not_8_out, not_9_out);
  not not_9 (not_9_out, C7);
  not not_10 (not_10_out, C1);
  or or_10 (or_10_out, not_10_out, not_11_out);
  not not_11 (not_11_out, C8);
  not not_12 (not_12_out, C1);
  or or_11 (or_11_out, not_12_out, C2, not_13_out);
  not not_13 (not_13_out, C4);
  not not_14 (not_14_out, C1);
  or or_12 (or_12_out, not_14_out, C3, not_15_out);
  not not_15 (not_15_out, C4);
  not not_16 (not_16_out, C1);
  not not_17 (not_17_out, C2);
  not not_18 (not_18_out, C3);
  not not_19 (not_19_out, C4);
  not not_20 (not_20_out, C5);
  not not_21 (not_21_out, C6);
  not not_22 (not_22_out, C1);
  not not_23 (not_23_out, C2);
  not not_24 (not_24_out, C3);
  not not_25 (not_25_out, C4);
  not not_26 (not_26_out, C5);
  not not_27 (not_27_out, C1);
  not not_28 (not_28_out, C2);
  not not_29 (not_29_out, C3);
  not not_30 (not_30_out, C4);
  not not_31 (not_31_out, C8);
  not not_32 (not_32_out, C1);
  not not_33 (not_33_out, C2);
  not not_34 (not_34_out, C3);
  not not_35 (not_35_out, C4);
  not not_36 (not_36_out, C1);
  not not_37 (not_37_out, C2);
  not not_38 (not_38_out, C3);
  not not_39 (not_39_out, C4);
  not not_40 (not_40_out, C7);
  not not_41 (not_41_out, C8);
  not not_42 (not_42_out, C1);
  not not_43 (not_43_out, C2);
  not not_44 (not_44_out, C5);
  not not_45 (not_45_out, C6);
  not not_46 (not_46_out, C7);
  not not_47 (not_47_out, C8);
  not not_48 (not_48_out, C1);
  not not_49 (not_49_out, C2);
  not not_50 (not_50_out, C6);
  not not_51 (not_51_out, C7);
  not not_52 (not_52_out, C8);
  not not_53 (not_53_out, C1);
  not not_54 (not_54_out, C3);
  not not_55 (not_55_out, C4);
  not not_56 (not_56_out, C5);
  not not_57 (not_57_out, C6);
  not not_58 (not_58_out, C7);
  not not_59 (not_59_out, C8);
  not not_60 (not_60_out, C1);
  not not_61 (not_61_out, C1);
  not not_62 (not_62_out, C2);
  not not_63 (not_63_out, C3);
  not not_64 (not_64_out, C4);
  not not_65 (not_65_out, C5);
  not not_66 (not_66_out, C6);
  not not_67 (not_67_out, C7);
  not not_68 (not_68_out, C8);
  not not_69 (not_69_out, C1);
  not not_70 (not_70_out, C2);
  not not_71 (not_71_out, C3);
  not not_72 (not_72_out, C6);
  not not_73 (not_73_out, C7);
  not not_74 (not_74_out, C8);
  and and_1 (and_1_out, not_16_out, not_17_out, not_18_out, not_19_out, not_20_out, not_21_out, C8);
  and and_2 (and_2_out, not_22_out, not_23_out, not_24_out, not_25_out, not_26_out, C7);
  and and_3 (and_3_out, not_27_out, not_28_out, not_29_out, not_30_out, C6, not_31_out);
  and and_4 (and_4_out, not_32_out, not_33_out, not_34_out, not_35_out, C6, C7);
  and and_5 (and_5_out, not_36_out, not_37_out, not_38_out, not_39_out, C5, not_40_out, not_41_out);
  and and_6 (and_6_out, not_42_out, not_43_out, C3, not_44_out, not_45_out, not_46_out, not_47_out);
  and and_7 (and_7_out, not_48_out, not_49_out, C3, C4, not_50_out, not_51_out, not_52_out);
  and and_8 (and_8_out, not_53_out, C2, not_54_out, not_55_out, not_56_out, not_57_out, not_58_out, not_59_out);
  and and_9 (and_9_out, not_60_out, C2, C3, C4, C5, C6, C7, C8);
  and and_10 (and_10_out, not_61_out, not_62_out, not_63_out, not_64_out, not_65_out, not_66_out, not_67_out, not_68_out);
  and and_11 (and_11_out, not_69_out, not_70_out, not_71_out, C4, C5, not_72_out, not_73_out, not_74_out);
  and and_12 (TG, or_1_out, or_2_out, or_3_out, or_4_out, or_5_out, or_6_out, or_7_out, or_8_out, or_9_out, or_10_out, or_11_out, or_12_out);
  or or_13 (TD, and_1_out, and_2_out, and_3_out, and_4_out, and_5_out, and_6_out, and_7_out, and_8_out, and_9_out);
  or or_14 (A, and_10_out, and_11_out);

  assign R = 1'b0;
endmodule
