// Logisim project WOW SUPER.circ as structural Verilog: 2 circuits, main circuit main
module main (
  input  in_1,
  input  in_2,
  input  in_3,
  input  in_4,
  input  in_5,
  input  in_6,
  input  in_7,
  input  in_8,
  output out_9,
  output S1,
  output S2,
  output out_12,
  output OVERFLOW
);

  wire addition_1_r_2, addition_2_r_2, addition_3_r_2;

  Addition addition_1 (.A(in_1), .B(in_5), .r(1'b0), .S(out_9), .R_2(addition_1_r_2));
  Addition addition_2 (.A(in_2), .B(in_6), .r(addition_1_r_2), .S(S1), .R_2(addition_2_r_2));
  Addition addition_3 (.A(in_3), .B(in_7), .r(addition_2_r_2), .S(S2), .R_2(addition_3_r_2));
  Addition addition_4 (.A(in_4), .B(in_8), .r(addition_3_r_2), .S(out_12), .R_2(OVERFLOW));
endmodule

module Addition (
  input  A,
  input  B,
  input  r,
  output S,
  output R_2
);

  wire and_1_out, and_2_out, and_3_out, and_4_out, and_5_out, and_6_out, and_7_out, not_1_out, not_2_out,
       not_3_out, not_4_out, not_5_out, not_6_out;

  not not_1 (not_1_out, A);
  not not_2 (not_2_out, B);
  not not_3 (not_3_out, A);
  not not_4 (not_4_out, r);
  not not_5 (not_5_out, B);
  not not_6 (not_6_out, r);
  and and_1 (and_1_out, B, r);
  and and_2 (and_2_out, A, r);
  and and_3 (and_3_out, A, B);
  and and_4 (and_4_out, not_1_out, not_2_out, r);
  and and_5 (and_5_out, not_3_out, B, not_4_out);
  and and_6 (and_6_out, A, not_5_out, not_6_out);
  and and_7 (and_7_out, A, B, r);
  or or_1 (R_2, and_1_out, and_2_out, and_3_out);
  or or_2 (S, and_4_out, and_5_out, and_6_out, and_7_out);
endmodule
